// Logisim project jrmips.circ as structural Verilog: 8 circuits, main circuit main
module main (
);

  wire alu_2_1_positive_output, alu_2_1_zero_output, and_1_out, and_2_out, and_3_out, clock_1_out,
       decoder_1_1_b, decoder_1_1_bx, decoder_1_1_bz, decoder_1_1_jal, decoder_1_1_jr, decoder_1_1_put,
       decoder_1_1_regwrite, decoder_2_1_halt, decoder_2_1_memread, decoder_2_1_memsel, decoder_2_1_memtoreg,
       decoder_2_1_memwrite, fields_1_subop, not_1_out, or_1_out, register_2_q;
  wire [1:0] decoder_1_1_alusrc0;
  wire [2:0] decoder_1_1_aluop0, fields_1_rs, fields_1_rt;
  wire [3:0] fields_1_opcode, register_3_q, register_3_q_2, register_3_q_3, register_3_q_4;
  wire [7:0] adder_1_out, bitselector_1_out, bitselector_2_out, multiplexer_5_out, register_1_q;
  wire [15:0] alu_2_1_alu_output, bit_extender_1_out, bit_extender_2_out, fields_1_imm, fields_1_shamt,
       multiplexer_1_out, multiplexer_2_out, multiplexer_3_out, multiplexer_4_out, multiplexer_6_out,
       ram_1_data, register_file_1_read_data_1, register_file_1_read_data_2, rom_1_data;

  and and_1 (and_1_out, clock_1_out, not_1_out);
  Clock clock_1 (.out(clock_1_out));
  not not_1 (not_1_out, register_2_q);
  Register register_1 (.D(multiplexer_5_out), .Q(register_1_q), .clk(and_1_out));  // open: en, clr
  LED Halt_LED (.in(register_2_q));
  Register #(.width(1)) register_2 (
    .D(decoder_2_1_halt), .en(decoder_2_1_halt), .Q(register_2_q), .clk(and_1_out));  // open: clr
  Adder adder_1 (.a(8'h1), .b(register_1_q), .out(adder_1_out));  // open: cin, cout
  Fields fields_1 (
    .Opcode(fields_1_opcode), .RS(fields_1_rs), .RT(fields_1_rt), .Subop(fields_1_subop),
    .Shamt(fields_1_shamt), .Input(rom_1_data), .Imm(fields_1_imm));
  ROM #(.dataWidth(16)) rom_1 (.addr(register_1_q), .data(rom_1_data));  // open: sel
  assign bit_extender_1_out = {{8{1'b0}}, adder_1_out};  // Bit_Extender bit_extender_1
  assign bit_extender_2_out = {{8{bitselector_1_out[7]}}, bitselector_1_out};  // Bit_Extender bit_extender_2
  BitSelector #(.width(16), .group(8)) bitselector_1 (.in(fields_1_imm), .out(bitselector_1_out), .sel(1'b0));
  Multiplexer #(.width(16), .enable("false")) multiplexer_1 (
    .in0(bit_extender_2_out), .in1(fields_1_imm), .out(multiplexer_1_out), .sel(fields_1_subop));
  Hex_Digit_Display hex_digit_display_1 (.value(register_3_q_4));  // open: dp
  Multiplexer #(.width(16), .enable("false")) multiplexer_2 (
    .in0(multiplexer_6_out), .in1(bit_extender_1_out), .out(multiplexer_2_out), .sel(decoder_1_1_jal));
  Decoder_1 decoder_1_1 (
    .op3(fields_1_opcode[3]), .op2(fields_1_opcode[2]), .op1(fields_1_opcode[1]), .op0(fields_1_opcode[0]),
    .sub(fields_1_subop), .jal(decoder_1_1_jal), .regwrite(decoder_1_1_regwrite),
    .alusrc1(decoder_1_1_alusrc0[1]), .alusrc0(decoder_1_1_alusrc0[0]), .put(decoder_1_1_put),
    .jr(decoder_1_1_jr), .aluop2(decoder_1_1_aluop0[2]), .aluop1(decoder_1_1_aluop0[1]),
    .aluop0(decoder_1_1_aluop0[0]), .bx(decoder_1_1_bx), .bz(decoder_1_1_bz), .b(decoder_1_1_b));
  Decoder_2 decoder_2_1 (
    .op3(fields_1_opcode[3]), .op2(fields_1_opcode[2]), .op1(fields_1_opcode[1]), .op0(fields_1_opcode[0]),
    .sub(fields_1_subop), .memwrite(decoder_2_1_memwrite), .memsel(decoder_2_1_memsel),
    .memread(decoder_2_1_memread), .memtoreg(decoder_2_1_memtoreg), .halt(decoder_2_1_halt));
  Hex_Digit_Display hex_digit_display_2 (.value(register_3_q_2));  // open: dp
  Hex_Digit_Display hex_digit_display_3 (.value(register_3_q_3));  // open: dp
  Hex_Digit_Display hex_digit_display_4 (.value(register_3_q));  // open: dp
  Register #(.width(16)) register_3 (
    .D(register_file_1_read_data_1), .en(decoder_1_1_put),
    .Q({register_3_q_4, register_3_q_3, register_3_q_2, register_3_q}), .clk(and_1_out));  // open: clr
  Register_File register_file_1 (
    .Register_Write(decoder_1_1_regwrite), .Clock(and_1_out), .Read_Data_1(register_file_1_read_data_1),
    .Read_Register_1(fields_1_rs), .Read_Data_2(register_file_1_read_data_2), .Read_Register_2(fields_1_rt),
    .Write_Data(multiplexer_2_out), .Write_Register(fields_1_rs));
  Multiplexer #(.width(16), .enable("false")) multiplexer_3 (
    .in0(multiplexer_1_out), .in1(register_file_1_read_data_1), .out(multiplexer_3_out), .sel(decoder_1_1_jr));
  Multiplexer #(.select(2), .width(16), .enable("false")) multiplexer_4 (
    .in0(register_file_1_read_data_2), .in1(multiplexer_1_out), .in2(fields_1_shamt),
    .out(multiplexer_4_out), .sel(decoder_1_1_alusrc0));  // open: in3
  BitSelector #(.width(16), .group(8)) bitselector_2 (.in(multiplexer_3_out), .out(bitselector_2_out), .sel(1'b0));
  ALU_2 alu_2_1 (
    .ALU_Output(alu_2_1_alu_output), .Positive_Output(alu_2_1_positive_output),
    .Zero_Output(alu_2_1_zero_output), .A(register_file_1_read_data_1), .B(multiplexer_4_out),
    .ALU_Control(decoder_1_1_aluop0));
  and and_2 (and_2_out, alu_2_1_positive_output, decoder_1_1_bx);
  and and_3 (and_3_out, alu_2_1_zero_output, decoder_1_1_bz);
  Multiplexer #(.width(8), .enable("false")) multiplexer_5 (
    .in0(adder_1_out), .in1(bitselector_2_out), .out(multiplexer_5_out), .sel(or_1_out));
  or or_1 (or_1_out, and_2_out, and_3_out, decoder_1_1_b);
  Multiplexer #(.width(16), .enable("false")) multiplexer_6 (
    .in0(alu_2_1_alu_output), .in1(ram_1_data), .out(multiplexer_6_out), .sel(decoder_2_1_memtoreg));
  RAM #(.addrWidth(16), .dataWidth(16), .bus("separate")) ram_1 (
    .addr(register_file_1_read_data_2), .din(register_file_1_read_data_1), .data(ram_1_data),
    .str(decoder_2_1_memwrite), .sel(decoder_2_1_memsel), .clk(and_1_out), .ld(decoder_2_1_memread));  // open: clr

  // Notes on the sheet:
  //   contents of rom_1 (hex, n*v repeats v):
  //   1001 201e 4018 0 4009 0 4009 0 4009 0 f000
  //   tgh19@pitt.edu
  //   by: Thomas Hoffman  
endmodule

// Registers
module Register_File (
  input  [15:0] Write_Data,
  input  Register_Write,
  input  [2:0] Read_Register_1,
  input  [2:0] Write_Register,
  input  [2:0] Read_Register_2,
  input  Clock,
  output [15:0] Read_Data_1,
  output [15:0] Read_Data_2
);

  wire demultiplexer_1_out0, demultiplexer_1_out1, demultiplexer_1_out2, demultiplexer_1_out3,
       demultiplexer_1_out4, demultiplexer_1_out5, demultiplexer_1_out6, demultiplexer_1_out7;
  wire [15:0] r0_q, r1_q, r2_q, r3_q, r4_q, r5_q, r6_q, r7_q;

  Demultiplexer #(.select(3), .disabled(0)) demultiplexer_1 (
    .out0(demultiplexer_1_out0), .out1(demultiplexer_1_out1), .out2(demultiplexer_1_out2),
    .out3(demultiplexer_1_out3), .out4(demultiplexer_1_out4), .out5(demultiplexer_1_out5),
    .out6(demultiplexer_1_out6), .out7(demultiplexer_1_out7), .in(Register_Write), .sel(Write_Register),
    .en(Register_Write));
  Register #(.width(16)) r0 (.D(Write_Data), .en(demultiplexer_1_out0), .Q(r0_q), .clk(Clock));  // open: clr
  Register #(.width(16)) r1 (.D(Write_Data), .en(demultiplexer_1_out1), .Q(r1_q), .clk(Clock));  // open: clr
  Register #(.width(16)) r2 (.D(Write_Data), .en(demultiplexer_1_out2), .Q(r2_q), .clk(Clock));  // open: clr
  Register #(.width(16)) r3 (.D(Write_Data), .en(demultiplexer_1_out3), .Q(r3_q), .clk(Clock));  // open: clr
  Register #(.width(16)) r4 (.D(Write_Data), .en(demultiplexer_1_out4), .Q(r4_q), .clk(Clock));  // open: clr
  Register #(.width(16)) r5 (.D(Write_Data), .en(demultiplexer_1_out5), .Q(r5_q), .clk(Clock));  // open: clr
  Register #(.width(16)) r6 (.D(Write_Data), .en(demultiplexer_1_out6), .Q(r6_q), .clk(Clock));  // open: clr
  Register #(.width(16)) r7 (.D(Write_Data), .en(demultiplexer_1_out7), .Q(r7_q), .clk(Clock));  // open: clr
  Multiplexer #(.select(3), .width(16), .enable("false")) multiplexer_1 (
    .in0(r0_q), .in1(r1_q), .in2(r2_q), .in3(r3_q), .in4(r4_q), .in5(r5_q), .in6(r6_q), .in7(r7_q),
    .out(Read_Data_1), .sel(Read_Register_1));
  Multiplexer #(.select(3), .width(16), .enable("false")) multiplexer_2 (
    .in0(r0_q), .in1(r1_q), .in2(r2_q), .in3(r3_q), .in4(r4_q), .in5(r5_q), .in6(r6_q), .in7(r7_q),
    .out(Read_Data_2), .sel(Read_Register_2));
endmodule

module ALU (
  input  [15:0] A,
  input  [15:0] B,
  input  [1:0] ALU_Control,
  output [15:0] ALU_Result
);

  wire [15:0] adder_1_out, and_1_out, nor_1_out, subtractor_1_out;

  Adder #(.width(16)) adder_1 (.a(A), .b(B), .out(adder_1_out));  // open: cin, cout
  Subtractor #(.width(16)) subtractor_1 (.a(A), .b(B), .out(subtractor_1_out));  // open: bin, bout
  assign and_1_out = A & B;  // AND_Gate and_1, 16 bits wide
  assign nor_1_out = ~(A | B);  // NOR_Gate nor_1, 16 bits wide
  Multiplexer #(.select(2), .width(16), .enable("false")) multiplexer_1 (
    .in0(adder_1_out), .in1(subtractor_1_out), .in2(and_1_out), .in3(nor_1_out), .out(ALU_Result),
    .sel(ALU_Control));
endmodule

module ALU_2 (
  input  [15:0] A,
  input  [15:0] B,
  input  [2:0] ALU_Control,
  output [15:0] ALU_Output,
  output Positive_Output,
  output Zero_Output
);

  wire [15:0] adder_1_out, and_1_out, nor_1_out, shifter_1_left_shift_result, shifter_1_right_shift_result,
       subtractor_1_out;

  Adder #(.width(16)) adder_1 (.a(A), .b(B), .out(adder_1_out));  // open: cin, cout
  Subtractor #(.width(16)) subtractor_1 (.a(A), .b(B), .out(subtractor_1_out));  // open: bin, bout
  assign and_1_out = A & B;  // AND_Gate and_1, 16 bits wide
  assign nor_1_out = ~(A | B);  // NOR_Gate nor_1, 16 bits wide
  Shifter shifter_1 (
    .Input(A), .Shamt(B), .Left_Shift_Result(shifter_1_left_shift_result),
    .Right_Shift_Result(shifter_1_right_shift_result));
  Comparator #(.width(16)) comparator_1 (.a(A), .b({16{1'b0}}), .gt(Positive_Output), .eq(Zero_Output));  // open: lt
  Multiplexer #(.select(3), .width(16), .enable("false")) multiplexer_1 (
    .in0(adder_1_out), .in1(subtractor_1_out), .in2(and_1_out), .in3(nor_1_out),
    .in4(shifter_1_left_shift_result), .in5(shifter_1_right_shift_result), .out(ALU_Output), .sel(ALU_Control));  // open: in6, in7
endmodule

module Fields (
  input  [15:0] Input,
  output [3:0] Opcode,
  output Subop,
  output [2:0] RS,
  output [15:0] Shamt,
  output [2:0] RT,
  output [15:0] Imm
);

  assign Shamt = {{12{1'b0}}, Input[4:1]};  // Bit_Extender bit_extender_1
  assign Imm = {{8{1'b0}}, Input[8:1]};  // Bit_Extender bit_extender_2

  assign Opcode = Input[15:12];
  assign RS = Input[11:9];
  assign RT = Input[8:6];
  assign Subop = Input[0];
endmodule

module Shifter (
  input  [15:0] Input,
  input  [15:0] Shamt,
  output [15:0] Left_Shift_Result,
  output [15:0] Right_Shift_Result
);

  wire [3:0] bit_extender_1_out;

  Bit_Extender #(.in_width(16), .out_width(4)) bit_extender_1 (.in(Shamt), .out(bit_extender_1_out));
  Shifter_part #(.width(16)) shifter_1 (.in(Input), .\dist (bit_extender_1_out), .out(Left_Shift_Result));
  Shifter_part #(.width(16), .shift("lr")) shifter_2 (
    .in(Input), .\dist (bit_extender_1_out), .out(Right_Shift_Result));
endmodule

module Decoder_1 (
  input  op3,
  input  op2,
  input  op1,
  input  op0,
  input  sub,
  output jal,
  output regwrite,
  output alusrc1,
  output alusrc0,
  output put,
  output jr,
  output aluop2,
  output aluop1,
  output aluop0,
  output bx,
  output bz,
  output b
);

  wire and_2_out, and_3_out, and_4_out, and_5_out, and_6_out, and_7_out, and_9_out, and_10_out, and_13_out,
       and_14_out, not_1_out, not_2_out, not_3_out, not_4_out, not_5_out, not_6_out, not_7_out, not_8_out,
       not_9_out, not_10_out, not_11_out, not_12_out, not_13_out, not_14_out, not_15_out, not_16_out,
       not_17_out, not_18_out;

  not not_1 (not_1_out, op3);
  not not_2 (not_2_out, op2);
  not not_3 (not_3_out, op3);
  not not_4 (not_4_out, op2);
  not not_5 (not_5_out, op2);
  not not_6 (not_6_out, op3);
  not not_7 (not_7_out, op1);
  not not_8 (not_8_out, op3);
  not not_9 (not_9_out, sub);
  not not_10 (not_10_out, op2);
  not not_11 (not_11_out, op0);
  not not_12 (not_12_out, op0);
  and and_1 (aluop1, op1, op0);
  not not_13 (not_13_out, op1);
  not not_14 (not_14_out, op0);
  not not_15 (not_15_out, op2);
  not not_16 (not_16_out, op2);
  not not_17 (not_17_out, op1);
  and and_2 (and_2_out, not_1_out, not_2_out, op0);
  and and_3 (and_3_out, not_3_out, not_4_out, op1);
  and and_4 (and_4_out, not_5_out, op1, op0);
  and and_5 (and_5_out, not_6_out, op2, not_7_out);
  and and_6 (and_6_out, not_8_out, op2, not_9_out);
  and and_7 (and_7_out, not_10_out, not_11_out);
  not not_18 (not_18_out, put);
  nor nor_1 (put, op3, op2, op1, op0, sub);
  and and_8 (jr, op1, not_12_out);
  and and_9 (and_9_out, not_13_out, sub);
  and and_10 (and_10_out, op0, sub);
  and and_11 (bx, op3, not_14_out);
  and and_12 (bz, op3, not_15_out, op0);
  and and_13 (and_13_out, op3, not_16_out, op1);
  and and_14 (and_14_out, op3, op2, not_17_out);
  or or_1 (regwrite, and_2_out, and_3_out, and_4_out, and_5_out, and_6_out);
  and and_15 (alusrc0, and_7_out, not_18_out);
  or or_2 (aluop0, and_9_out, and_10_out);
  or or_3 (b, and_13_out, and_14_out);

  assign aluop2 = op2;
  assign alusrc1 = op2;
  assign jal = op3;
endmodule

module Decoder_2 (
  input  op3,
  input  op2,
  input  op1,
  input  op0,
  input  sub,
  output memwrite,
  output memsel,
  output memread,
  output memtoreg,
  output halt
);

  wire not_1_out, not_2_out, not_3_out, not_4_out, not_5_out, not_6_out;

  not not_1 (not_1_out, op3);
  not not_2 (not_2_out, op3);
  not not_3 (not_3_out, op3);
  not not_4 (not_4_out, sub);
  not not_5 (not_5_out, op3);
  not not_6 (not_6_out, sub);
  and and_1 (halt, op3, op2, op1);
  and and_2 (memwrite, not_1_out, op2, op1, sub);
  and and_3 (memsel, not_2_out, op2, op1);
  and and_4 (memread, not_3_out, op2, op1, not_4_out);
  and and_5 (memtoreg, not_5_out, op2, op1, not_6_out);
endmodule
